# Fritzing sketch Arduino Solenoid With Placeholder Power Supply (saved by Fritzing 0.9.3b)
breadboards: 1

parts:
  Q2 = MOSFET-NCHANNEL [part_number=FQP30N06L package=to220v]
  L1 = Solenoid  # not connected
  VCC1 = Battery block 9V [part_number="Actually 12v"]
  D1 = Diode [package=diode-hv]
  R1 = Resistor [tolerance=±5% resistance=330 package=THT]
  3_3V_REGULATOR = Voltage Regulator [package=78xxl]
  J2 = JST-B3P-VH [part_number="ARDUINO 1=3.3v, 2=GND, 3=PWM" package=THT]
  R2 = Resistor [tolerance=±5% resistance=1k package=THT]

nets:
  N1: Q2.G, R1.Pin_1
  N2: Q2.D, D1.A
  N3: Q2.S, VCC1.-
  N4: VCC1.+, D1.C, 3_3V_REGULATOR.IN
  N5: R1.Pin_0, J2.pin3, R2.Pin_1
  N6: 3_3V_REGULATOR.GND, J2.pin2, R2.Pin_0
  N7: 3_3V_REGULATOR.OUT, J2.pin1
