# Fritzing sketch Arduino Solenoid (saved by Fritzing 0.9.3b)
circuit board: 8.46667cm x 5.64444cm
breadboards: 1

parts:
  Q2 = MOSFET-NCHANNEL [part_number=FQP30N06L package=to220v]
  VCC1 = Battery block 9V [part_number="Actually 12v"]
  D1 = Diode [package=diode-hv]
  J2 = JST-B3P-VH [part_number="ARDUINO 1=3.3v, 2=GND, 3=PWM" package=THT]
  R1 = Resistor [tolerance=±5% resistance=330 package=THT]
  R2 = Resistor [tolerance=±5% resistance=1k package=THT]
  L1 = Solenoid

nets:
  N1: Q2.G, R1.Pin_1
  N2: Q2.D, D1.A, L1.pin1
  N3: Q2.S, VCC1.-
  N4: VCC1.+, D1.C, L1.pin2
  N5: J2.pin2, R2.Pin_0
  N6: J2.pin3, R1.Pin_0, R2.Pin_1
