# Fritzing sketch Both Solenoids (saved by Fritzing 0.9.3b)
circuit board: 8.46667cm x 5.64444cm
breadboards: 1

parts:
  Q2 = MOSFET-NCHANNEL [part_number=FQP30N06L package=to220v]
  Car_Battery = Battery block 9V [part_number="Actually 12v"]
  D1 = Diode [package=diode-hv]
  R1 = Resistor [tolerance=±5% resistance=330 package=THT]
  R2 = Resistor [tolerance=±5% resistance=1k package=THT]
  L1 = Solenoid
  L2 = Solenoid
  Q3 = MOSFET-NCHANNEL [part_number=FQP30N06L package=to220v]
  R3 = Resistor [tolerance=±5% resistance=330 package=THT]
  R4 = Resistor [tolerance=±5% resistance=1k package=THT]
  Arduino = JST-B3P-VH [part_number="1=GND, 2=PWM1, 3=PWM2" package=THT]
  D2 = Diode [package=diode-hv]

nets:
  N1: Q2.G, R1.Pin_1
  N2: Q2.D, D1.A, L1.pin2
  N3: Q2.S, Q3.S
  N4: Car_Battery.-, R2.Pin_0, R4.Pin_0, Arduino.pin1
  N5: Car_Battery.+, D1.C, L1.pin1, L2.pin1, D2.C
  N6: R1.Pin_0, R2.Pin_1, Arduino.pin2
  N7: L2.pin2, Q3.D, D2.A
  N8: Q3.G, R3.Pin_1
  N9: R3.Pin_0, R4.Pin_1, Arduino.pin3
